# Fritzing sketch TLCv1 (saved by Fritzing 0.9.3b)
circuit board: 7.42576cm x 4.80733cm
breadboards: 1

parts:
  Status = RGB LED (com. cathode, rbg) [package="5 mm [THT]"]
  Effect_Toggle = Header 2 [package=molex-1x2_lock]
  Pwr_Swtch = Header 2 [package=molex-1x2_lock]
  Power_5-12v = Header 2 [package=molex-1x2_lock]
  Config = DIP Switch 4 Position [package=dipswitch-04]
  3_3v_o_5v = female pin header, 3 pins [form="♀ (female)"]
  G = Resistor [tolerance=±5% resistance=220 package="0603 [SMD]"]
  R = Resistor [tolerance=±5% resistance=220 package="0603 [SMD]"]
  B = Resistor [tolerance=±5% resistance=220 package="0603 [SMD]"]
  LED_Strip = Header 3 [package=molex-1x3_lock]
  100uf = Capacitor Polarized [package=cpol-radial-100uf-25v]
  Pulse_Sensor = Header 3 [package=molex-1x3_lock]
  J2 = female pin header, 15 pins [form="♀ (female)"]  # not connected
  Nano = Arduino Nano (Rev3.0)
  J3 = Generic shrouded header - 8 pins [form="♂ (shrouded male)" package=THT]

nets:
  N1: Status.red_anode, R.Pin_1
  N2: Status.common_cathode, Effect_Toggle.2, Power_5-12v.2, Config.5, Config.6, Config.7, Config.8, LED_Strip.3, 100uf.-, Pulse_Sensor.1, Nano.GND, J3.grd
  N3: Status.blue_anode, G.Pin_1
  N4: Status.green_anode, B.Pin_1
  N5: Effect_Toggle.1, Nano.D6
  N6: Pwr_Swtch.1, Nano.VIN
  N7: Pwr_Swtch.2, Power_5-12v.1
  N8: Config.1, Nano.D2
  N9: Config.2, Nano.D3
  N10: Config.3, Nano.D4
  N11: Config.4, Nano.D5
  N12: 3_3v_o_5v.pin1, Nano.3V3
  N13: 3_3v_o_5v.pin2, 100uf.+, J3.v+
  N14: 3_3v_o_5v.pin3, LED_Strip.1, Pulse_Sensor.2, Nano.5V
  N15: G.Pin_0, Nano.A1
  N16: R.Pin_0, Nano.A0
  N17: B.Pin_0, Nano.A2
  N18: LED_Strip.2, Nano.D8
  N19: Pulse_Sensor.3, Nano.A7
  N20: Nano.D9, J3.ce
  N21: Nano.D10, J3.csn
  N22: Nano.D11/MOSI, J3.mosi
  N23: Nano.D12/MISO, J3.miso
  N24: Nano.D13/SCK, J3.sck

custom parts:
  Generic shrouded header - 8 pins: Generic shrouded header
